# Fritzing sketch piano (saved by Fritzing 0.9.10b)
circuit board: 8.47cm x 5.64cm
breadboards: 1

parts:
  Nodemcu = Amica NodeMCU DEVKIT 1.0
  J1 = female pin header, 5 pins [form="♀ (female)"]
  J2 = female pin header, 7 pins [form="♀ (female)"]
  J3 = female pin header, 5 pins [form="♀ (female)"]
  J4 = female pin header, 7 pins [form="♀ (female)"]
  MPR121_1 = Adafruit MPR121
  MPR121_2 = Adafruit MPR121

nets:
  GND: Nodemcu.pin2, Nodemcu.pin_9, Nodemcu.pin_25, MPR121_1.GND, MPR121_2.GND
  N1: Nodemcu.pin_13, MPR121_1.SDA, MPR121_2.SDA
  N2: Nodemcu.pin_14, MPR121_1.SCL, MPR121_2.SCL
  VIN: Nodemcu.pin_30, MPR121_1.VIN, MPR121_2.VIN
  N3: J1.pin1, MPR121_1.ELEC0
  N4: J1.pin2, MPR121_1.ELEC1
  N5: J1.pin3, MPR121_1.ELEC2
  N6: J1.pin4, MPR121_1.ELEC3
  N7: J1.pin5, MPR121_1.ELEC4
  N8: J2.pin1, MPR121_1.ELEC5
  N9: J2.pin2, MPR121_1.ELEC6
  N10: J2.pin3, MPR121_1.ELEC7
  N11: J2.pin4, MPR121_1.ELEC8
  N12: J2.pin5, MPR121_1.ELEC9
  N13: J2.pin6, MPR121_1.ELEC10
  N14: J2.pin7, MPR121_1.ELEC11
  N15: J3.pin1, MPR121_2.ELEC0
  N16: J3.pin2, MPR121_2.ELEC1
  N17: J3.pin3, MPR121_2.ELEC2
  N18: J3.pin4, MPR121_2.ELEC3
  N19: J3.pin5, MPR121_2.ELEC4
  N20: J4.pin1, MPR121_2.ELEC5
  N21: J4.pin2, MPR121_2.ELEC6
  N22: J4.pin3, MPR121_2.ELEC7
  N23: J4.pin4, MPR121_2.ELEC8
  N24: J4.pin5, MPR121_2.ELEC9
  N25: J4.pin6, MPR121_2.ELEC10
  N26: J4.pin7, MPR121_2.ELEC11

custom parts:
  Adafruit MPR121: Add lots of touch sensors to your next microcontroller project with this easy-to-use 12-channel capacitive touch sensor breakout board, starring the MPR121. This chip can handle up to 12 individual touch pads. The MPR121 has support for only I2C, which can be implemented with nearly any microcontroller. You can select one of 4 addresses with the ADDR pin, for a total of 48 capacitive touch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
